// Logisim project InfoCodeSchlossFinalv2.circ as structural Verilog
module main (
);

  wire _0, _0_2_out, _0_out, _1, _1_2_out, _1_out, _2, _2_2_out, _2_out, Eins, F1_falsch,
       Falsch_2_falschfolgend, Falsch_3_falschfolgend, Falsch__1_falsch, Falsch__2_falschfolgend,
       Falsch__3_falschfolgend, Falsch__4_falschfolgend, Falsch__last_falschfolgend, Falsch_falschfolgend,
       FalschWDHL, inputonce_1_taster_ausgang, Null, OK, R1_falsch, R1_richtig, R2_falsch, R2_richtig,
       R_0_falsch, R_0_richtig_2, Ready, Richtig__0_falsch, Richtig__0_richtig_2, Richtig__1_2_falsch,
       Richtig__1_2_richtig_2, Richtig__1_falsch, Richtig__1_richtig, Richtig__2_2_falsch,
       Richtig__2_2_richtig, Richtig__2_falsch, Richtig__2_richtig, richtig_zwei_zwei_1_falsch,
       richtig_zwei_zwei_1_richtig, speicher_2_out_4, Speicher_3_out_4, Speicher_4_out_4, speicher_5_out_4,
       Speicher_6_out_4, Speicher_7_out_4, Speicher_8_out_4, Speicher_9_out_4, speicher_10_out_4,
       Speicher_11_out_4, Speicher_12_out_4, speicher_13_out_4, Speicher_14_out_4, Speicher_15_out_4,
       Speicher_16_out_4, Speicher_out_4, Start, Start_2_out_5, Start_out, Takt, Takt_2_out, xor_1_out,
       xor_2_out, xor_3_out, xor_4_out, xor_5_out, xor_6_out, xor_7_out, xor_8_out, xor_9_out, xor_10_out,
       xor_11_out, xor_12_out, xor_13_out, xor_14_out, Zwei;

  Clock u_Takt (.out(Takt));
  Clock Takt_2 (.out(Takt_2_out));
  Button u_Start (.out(Start_out));
  Button u__0 (.out(_0_out));
  Button u__1 (.out(_1_out));
  Button u__2 (.out(_2_out));
  Button _0_2 (.out(_0_2_out));
  Button Start___Reset (.out(Start));
  Button _1_2 (.out(_1_2_out));
  D_Flip_Flop d_ff_1 (.clk(Takt_2_out), .D(Start_out));  // open: Q, Qn, preset, en, reset
  D_Flip_Flop d_ff_2 (.clk(Takt_2_out), .D(_0_out), .Q(_0));  // open: Qn, preset, en, reset
  D_Flip_Flop d_ff_3 (.clk(Takt_2_out), .D(_1_out), .Q(_1));  // open: Qn, preset, en, reset
  D_Flip_Flop d_ff_4 (.clk(Takt_2_out), .D(_2_out), .Q(_2));  // open: Qn, preset, en, reset
  Button _2_2 (.out(_2_2_out));
  InputOnce inputonce_1 (.Takt(Takt), .Taster_Input(Start), .Taster_Ausgang(inputonce_1_taster_ausgang));
  InputOnce inputonce_2 (.Takt(Takt), .Taster_Input(_0_2_out), .Taster_Ausgang(Null));
  InputOnce inputonce_3 (.Takt(Takt), .Taster_Input(_1_2_out), .Taster_Ausgang(Eins));
  InputOnce inputonce_4 (.Takt(Takt), .Taster_Input(_2_2_out), .Taster_Ausgang(Zwei));
  Richtig_Zwei R2 (.Null(_0), .Eins(_1), .Zwei(_2), .Richtig(R2_richtig), .Falsch(R2_falsch));  // open: InputStart
  Falsch_Eins F1 (.FalschvonRichtig(_0), .Null(_1), .Eins(_2), .Falsch(F1_falsch));  // open: Zwei
  ExactlyOne xor_1 (.out(xor_1_out), .in0(_2), .in1(_1), .in2(_0));
  ExactlyOne xor_2 (.out(xor_2_out), .in0(Null), .in1(Eins), .in2(Zwei));
  Richtig_Zwei Richtig__2 (
    .InputStart(Start_2_out_5), .Null(Null), .Eins(Eins), .Zwei(Zwei), .Richtig(Richtig__2_richtig),
    .Falsch(Richtig__2_falsch));
  ExactlyOne xor_3 (.out(xor_3_out), .in0(Null), .in1(Eins), .in2(Zwei));
  Speicher Speicher (.in_2(R2_richtig), .in_3(_1), .out_4(Speicher_out_4));  // open: in_1
  Speicher speicher_2 (.in_2(F1_falsch), .in_3(xor_1_out), .out_4(speicher_2_out_4));  // open: in_1
  Speicher_Start Start_2 (
    .in_1(Takt), .in_2(inputonce_1_taster_ausgang), .in_3(FalschWDHL), .in_4(xor_2_out),
    .out_5(Start_2_out_5), .Start_ausgang(Ready));
  Speicher Speicher_3 (.in_1(Takt), .in_2(Richtig__2_richtig), .in_3(xor_3_out), .out_4(Speicher_3_out_4));
  Falsch_Eins Falsch__1 (
    .FalschvonRichtig(Richtig__2_falsch), .Null(Null), .Eins(Eins), .Zwei(Zwei), .Falsch(Falsch__1_falsch));
  ExactlyOne xor_4 (.out(xor_4_out), .in0(_2), .in1(_1), .in2(_0));
  LED Wrong (.in(FalschWDHL));
  LED u_Ready (.in(Ready));
  Speicher Speicher_4 (.in_1(Takt), .in_2(Falsch__1_falsch), .in_3(xor_5_out), .out_4(Speicher_4_out_4));
  ExactlyOne xor_5 (.out(xor_5_out), .in0(Null), .in1(Eins), .in2(Zwei));
  Richtig_Eins R1 (.R2(Speicher_out_4), .Null(_0), .Eins(_1), .Zwei(_2), .Richtig(R1_richtig), .Falsch(R1_falsch));
  Falsch Falsch (
    .FalschvonRichtig(speicher_2_out_4), .FalschvonFalsch(R2_falsch), .Null(_0), .Eins(_1), .Zwei(_2),
    .FalschFolgend(Falsch_falschfolgend));
  Speicher speicher_5 (.in_2(Falsch_falschfolgend), .in_3(xor_4_out), .out_4(speicher_5_out_4));  // open: in_1
  LED u_OK (.in(OK));
  Richtig_Eins Richtig__1 (
    .R2(Speicher_3_out_4), .Null(Null), .Eins(Eins), .Zwei(Zwei), .Richtig(Richtig__1_richtig),
    .Falsch(Richtig__1_falsch));
  ExactlyOne xor_6 (.out(xor_6_out), .in0(Null), .in1(Eins), .in2(Zwei));
  Falsch Falsch__2 (
    .FalschvonRichtig(Richtig__1_falsch), .FalschvonFalsch(Speicher_4_out_4), .Null(Null), .Eins(Eins),
    .Zwei(Zwei), .FalschFolgend(Falsch__2_falschfolgend));
  Speicher Speicher_6 (.in_2(R1_richtig), .in_3(_2), .out_4(Speicher_6_out_4));  // open: in_1
  Speicher Speicher_7 (.in_1(Takt), .in_2(Richtig__1_richtig), .in_3(xor_6_out), .out_4(Speicher_7_out_4));
  ExactlyOne xor_7 (.out(xor_7_out), .in0(Null), .in1(Eins), .in2(Zwei));
  Falsch Falsch_2 (
    .FalschvonRichtig(speicher_5_out_4), .FalschvonFalsch(R1_falsch), .Null(_0), .Eins(_1), .Zwei(_2),
    .FalschFolgend(Falsch_2_falschfolgend));
  ExactlyOne xor_8 (.out(xor_8_out), .in0(_2), .in1(_1), .in2(_0));
  Richtig_Zwei_Zwei Richtig__2_2 (
    .R1(Speicher_7_out_4), .Null(Null), .Eins(Eins), .Zwei(Zwei), .Richtig(Richtig__2_2_richtig),
    .Falsch(Richtig__2_2_falsch));
  ExactlyOne xor_9 (.out(xor_9_out), .in0(Null), .in1(Eins), .in2(Zwei));
  Speicher Speicher_8 (.in_1(Takt), .in_2(Falsch__2_falschfolgend), .in_3(xor_7_out), .out_4(Speicher_8_out_4));
  Speicher Speicher_9 (.in_2(richtig_zwei_zwei_1_richtig), .in_3(_0), .out_4(Speicher_9_out_4));  // open: in_1
  Richtig_Zwei_Zwei richtig_zwei_zwei_1 (
    .R1(Speicher_6_out_4), .Null(_0), .Eins(_1), .Zwei(_2), .Richtig(richtig_zwei_zwei_1_richtig),
    .Falsch(richtig_zwei_zwei_1_falsch));
  Speicher speicher_10 (.in_2(Falsch_2_falschfolgend), .in_3(xor_8_out), .out_4(speicher_10_out_4));  // open: in_1
  Falsch Falsch__3 (
    .FalschvonRichtig(Richtig__2_2_falsch), .FalschvonFalsch(Speicher_8_out_4), .Null(Null), .Eins(Eins),
    .Zwei(Zwei), .FalschFolgend(Falsch__3_falschfolgend));
  ExactlyOne xor_10 (.out(xor_10_out), .in0(Null), .in1(Eins), .in2(Zwei));
  Falsch Falsch_3 (
    .FalschvonRichtig(speicher_10_out_4), .FalschvonFalsch(richtig_zwei_zwei_1_falsch), .Null(_0), .Eins(_1),
    .Zwei(_2), .FalschFolgend(Falsch_3_falschfolgend));
  ExactlyOne xor_11 (.out(xor_11_out), .in0(_2), .in1(_1), .in2(_0));
  Speicher Speicher_11 (.in_1(Takt), .in_2(Richtig__2_2_richtig), .in_3(xor_9_out), .out_4(Speicher_11_out_4));
  Speicher Speicher_12 (.in_1(Takt), .in_2(Falsch__3_falschfolgend), .in_3(xor_10_out), .out_4(Speicher_12_out_4));
  Richtig_Null R_0 (
    .Richtig(Speicher_9_out_4), .Null(_0), .Eins(_1), .Zwei(_2), .Richtig_2(R_0_richtig_2),
    .Falsch(R_0_falsch));
  Speicher speicher_13 (.in_2(Falsch_3_falschfolgend), .in_3(xor_11_out), .out_4(speicher_13_out_4));  // open: in_1
  Richtig_Null Richtig__0 (
    .Richtig(Speicher_11_out_4), .Null(Null), .Eins(Eins), .Zwei(Zwei), .Richtig_2(Richtig__0_richtig_2),
    .Falsch(Richtig__0_falsch));
  ExactlyOne xor_12 (.out(xor_12_out), .in0(Null), .in1(Eins), .in2(Zwei));
  ExactlyOne xor_13 (.out(xor_13_out), .in0(Null), .in1(Eins), .in2(Zwei));
  Speicher Speicher_14 (.in_2(R_0_richtig_2), .in_3(_1), .out_4(Speicher_14_out_4));  // open: in_1
  Speicher Speicher_15 (.in_1(Takt), .in_2(Richtig__0_richtig_2), .in_3(xor_12_out), .out_4(Speicher_15_out_4));
  Falsch Falsch__4 (
    .FalschvonRichtig(Richtig__0_falsch), .FalschvonFalsch(Speicher_12_out_4), .Null(Null), .Eins(Eins),
    .Zwei(Zwei), .FalschFolgend(Falsch__4_falschfolgend));
  Falsch Falsch_4 (
    .FalschvonRichtig(speicher_13_out_4), .FalschvonFalsch(R_0_falsch), .Null(_0), .Eins(_1), .Zwei(_2));  // open: FalschFolgend
  Speicher Speicher_16 (.in_1(Takt), .in_2(Falsch__4_falschfolgend), .in_3(xor_13_out), .out_4(Speicher_16_out_4));
  Richtig_Eins_Zwei Richtig__1_2 (
    .Richtig(Speicher_15_out_4), .Null(Null), .Eins(Eins), .Zwei(Zwei), .Richtig_2(Richtig__1_2_richtig_2),
    .Falsch(Richtig__1_2_falsch));
  Richtig_Eins_Zwei R1_2 (.Richtig(Speicher_14_out_4), .Null(_0), .Eins(_1), .Zwei(_2));  // open: Richtig_2, Falsch
  \Verzögerung  \verzögerung_1  (.Takt(Takt), .OK(Richtig__1_2_richtig_2), .Reset(Start), .Start_ausgang(OK));
  Falsch Falsch__last (
    .FalschvonRichtig(Richtig__0_falsch), .FalschvonFalsch(Speicher_16_out_4), .Null(Null), .Eins(Eins),
    .Zwei(Zwei), .FalschFolgend(Falsch__last_falschfolgend));
  xor xor_14 (xor_14_out, Richtig__1_2_falsch, Falsch__last_falschfolgend);
  \Verzögerung  \verzögerung_2  (.Takt(Takt), .OK(xor_14_out), .Reset(Start), .Start_ausgang(FalschWDHL));
endmodule

module Richtig_Zwei (
  input  InputStart,
  input  Null,
  input  Eins,
  input  Zwei,
  output Richtig,
  output Falsch
);

  wire and_2_out, and_3_out, not_1_out, not_2_out, not_3_out, not_4_out, not_5_out, not_6_out;

  not not_1 (not_1_out, Null);
  not not_2 (not_2_out, Eins);
  not not_3 (not_3_out, Null);
  not not_4 (not_4_out, Zwei);
  not not_5 (not_5_out, Eins);
  not not_6 (not_6_out, Zwei);
  and and_1 (Richtig, InputStart, not_1_out, not_2_out, Zwei);
  and and_2 (and_2_out, InputStart, not_3_out, Eins, not_4_out);
  or or_1 (Falsch, and_2_out, and_3_out);
  and and_3 (and_3_out, InputStart, Null, not_5_out, not_6_out);
endmodule

module Richtig_Eins (
  input  R2,
  input  Null,
  input  Eins,
  input  Zwei,
  output Richtig,
  output Falsch
);

  wire and_2_out, and_3_out, not_1_out, not_2_out, not_3_out, not_4_out, not_5_out, not_6_out;

  not not_1 (not_1_out, Null);
  not not_2 (not_2_out, Zwei);
  not not_3 (not_3_out, Null);
  not not_4 (not_4_out, Eins);
  not not_5 (not_5_out, Eins);
  not not_6 (not_6_out, Zwei);
  and and_1 (Richtig, R2, not_1_out, Eins, not_2_out);
  and and_2 (and_2_out, R2, not_3_out, not_4_out, Zwei);
  or or_1 (Falsch, and_2_out, and_3_out);
  and and_3 (and_3_out, R2, Null, not_5_out, not_6_out);
endmodule

module Richtig_Zwei_Zwei (
  input  R1,
  input  Null,
  input  Eins,
  input  Zwei,
  output Richtig,
  output Falsch
);

  wire and_2_out, and_3_out, not_1_out, not_2_out, not_3_out, not_4_out, not_5_out, not_6_out;

  not not_1 (not_1_out, Null);
  not not_2 (not_2_out, Eins);
  not not_3 (not_3_out, Null);
  not not_4 (not_4_out, Zwei);
  not not_5 (not_5_out, Eins);
  not not_6 (not_6_out, Zwei);
  and and_1 (Richtig, R1, not_1_out, not_2_out, Zwei);
  and and_2 (and_2_out, R1, not_3_out, Eins, not_4_out);
  or or_1 (Falsch, and_2_out, and_3_out);
  and and_3 (and_3_out, R1, Null, not_5_out, not_6_out);
endmodule

module Richtig_Null (
  input  Richtig,
  input  Null,
  input  Eins,
  input  Zwei,
  output Richtig_2,
  output Falsch
);

  wire and_2_out, and_3_out, not_1_out, not_2_out, not_3_out, not_4_out, not_5_out, not_6_out;

  not not_1 (not_1_out, Eins);
  not not_2 (not_2_out, Zwei);
  not not_3 (not_3_out, Null);
  not not_4 (not_4_out, Eins);
  not not_5 (not_5_out, Null);
  not not_6 (not_6_out, Zwei);
  and and_1 (Richtig_2, Richtig, Null, not_1_out, not_2_out);
  and and_2 (and_2_out, Richtig, not_3_out, not_4_out, Zwei);
  or or_1 (Falsch, and_2_out, and_3_out);
  and and_3 (and_3_out, Richtig, not_5_out, Eins, not_6_out);
endmodule

module Richtig_Eins_Zwei (
  input  Richtig,
  input  Null,
  input  Eins,
  input  Zwei,
  output Richtig_2,
  output Falsch
);

  wire and_2_out, and_3_out, not_1_out, not_2_out, not_3_out, not_4_out, not_5_out, not_6_out;

  not not_1 (not_1_out, Null);
  not not_2 (not_2_out, Zwei);
  not not_3 (not_3_out, Null);
  not not_4 (not_4_out, Eins);
  not not_5 (not_5_out, Eins);
  not not_6 (not_6_out, Zwei);
  and and_1 (Richtig_2, Richtig, not_1_out, Eins, not_2_out);
  and and_2 (and_2_out, Richtig, not_3_out, not_4_out, Zwei);
  or or_1 (Falsch, and_2_out, and_3_out);
  and and_3 (and_3_out, Richtig, Null, not_5_out, not_6_out);
endmodule

module Falsch_Eins (
  input  FalschvonRichtig,
  input  Null,
  input  Eins,
  input  Zwei,
  output Falsch
);

  wire and_1_out, and_2_out, not_1_out, not_2_out, not_3_out, not_4_out;

  not not_1 (not_1_out, Null);
  not not_2 (not_2_out, Zwei);
  not not_3 (not_3_out, Eins);
  not not_4 (not_4_out, Zwei);
  and and_1 (and_1_out, FalschvonRichtig, not_1_out, Eins, not_2_out);
  or or_1 (Falsch, and_1_out, and_2_out);
  and and_2 (and_2_out, FalschvonRichtig, Null, not_3_out, not_4_out);
endmodule

module Falsch (
  input  FalschvonRichtig,
  input  FalschvonFalsch,
  input  Null,
  input  Eins,
  input  Zwei,
  output FalschFolgend
);

  wire and_1_out, and_2_out, and_3_out, and_4_out, and_5_out, and_6_out, not_1_out, not_2_out, not_3_out,
       not_4_out, not_5_out, not_6_out, not_7_out, not_8_out, not_9_out, not_10_out, not_11_out, not_12_out;

  not not_1 (not_1_out, Eins);
  not not_2 (not_2_out, Zwei);
  not not_3 (not_3_out, Null);
  not not_4 (not_4_out, Zwei);
  not not_5 (not_5_out, Null);
  not not_6 (not_6_out, Eins);
  not not_7 (not_7_out, Eins);
  not not_8 (not_8_out, Zwei);
  not not_9 (not_9_out, Null);
  not not_10 (not_10_out, Zwei);
  not not_11 (not_11_out, Null);
  not not_12 (not_12_out, Eins);
  and and_1 (and_1_out, FalschvonRichtig, Null, not_1_out, not_2_out);
  and and_2 (and_2_out, FalschvonRichtig, not_3_out, Eins, not_4_out);
  and and_3 (and_3_out, FalschvonRichtig, not_5_out, not_6_out, Zwei);
  and and_4 (and_4_out, FalschvonFalsch, Null, not_7_out, not_8_out);
  and and_5 (and_5_out, FalschvonFalsch, not_9_out, Eins, not_10_out);
  and and_6 (and_6_out, FalschvonFalsch, not_11_out, not_12_out, Zwei);
  or or_1 (FalschFolgend, and_1_out, and_2_out, and_3_out, and_4_out, and_5_out, and_6_out);
endmodule

module Speicher (
  input  in_1,
  input  in_2,
  input  in_3,
  output out_4
);

  wire d_ff_1_q, d_ff_2_q, or_1_out, xor_1_out;

  xor xor_1 (xor_1_out, d_ff_2_q, out_4);
  D_Flip_Flop d_ff_1 (.clk(in_1), .D(or_1_out), .Q(d_ff_1_q));  // open: Qn, preset, en, reset
  or or_1 (or_1_out, in_2, xor_1_out);
  D_Flip_Flop d_ff_2 (.clk(in_1), .D(d_ff_1_q), .Q(d_ff_2_q));  // open: Qn, preset, en, reset
  and and_1 (out_4, d_ff_2_q, in_3);
endmodule

module Speicher_Start (
  input  in_1,
  input  in_2,
  input  in_3,
  input  in_4,
  output out_5,
  output Start_ausgang
);

  wire d_ff_1_q, or_1_out, xor_1_out, xor_2_out;

  buf xor_1 (xor_1_out, in_2);  // XOR_Gate
  or or_1 (or_1_out, xor_1_out, xor_2_out);
  xor xor_2 (xor_2_out, Start_ausgang, out_5);
  D_Flip_Flop d_ff_1 (.clk(in_1), .D(or_1_out), .Q(d_ff_1_q));  // open: Qn, preset, en, reset
  D_Flip_Flop d_ff_2 (.clk(in_1), .D(d_ff_1_q), .Q(Start_ausgang));  // open: Qn, preset, en, reset
  and and_1 (out_5, Start_ausgang, in_4);

  // Notes on the sheet:
  //   Absichtlich nicht verbunden
  //   Da sonst ready leuchte leuchtet
endmodule

module InputOnce (
  input  Takt,
  input  Taster_Input,
  output Taster_Ausgang
);

  wire d_ff_1_q, d_ff_2_q, d_ff_3_q;

  D_Flip_Flop d_ff_1 (.clk(Takt), .D(Taster_Input), .Q(d_ff_1_q));  // open: Qn, preset, en, reset
  D_Flip_Flop d_ff_2 (.clk(Takt), .D(d_ff_1_q), .Q(d_ff_2_q));  // open: Qn, preset, en, reset
  D_Flip_Flop d_ff_3 (.clk(Takt), .D(d_ff_2_q), .Q(d_ff_3_q));  // open: Qn, preset, en, reset
  ExactlyOne xor_1 (.out(Taster_Ausgang), .in0(d_ff_3_q), .in1(d_ff_3_q), .in2(d_ff_1_q));
endmodule

module \Verzögerung  (
  input  Takt,
  input  OK,
  input  Reset,
  output Start_ausgang
);

  wire and_1_out, and_2_out, d_ff_1_q, d_ff_1_qn, d_ff_2_q, d_ff_3_q, d_ff_3_qn, d_ff_4_q, d_ff_4_qn,
       d_ff_5_q, d_ff_5_qn, d_ff_6_q, d_ff_6_qn, d_ff_7_q, d_ff_7_qn, d_ff_8_q, d_ff_8_qn, d_ff_9_q,
       d_ff_10_q, d_ff_10_qn, d_ff_11_qn, not_1_out, not_2_out, or_1_out, xor_1_out;

  and and_1 (and_1_out, Takt, d_ff_9_q);
  D_Flip_Flop d_ff_1 (.clk(and_1_out), .D(d_ff_1_qn), .Q(d_ff_1_q), .Qn(d_ff_1_qn), .reset(Reset));  // open: preset, en
  D_Flip_Flop d_ff_2 (.clk(Takt), .D(Start_ausgang), .Q(d_ff_2_q), .reset(Reset));  // open: Qn, preset, en
  D_Flip_Flop d_ff_3 (.clk(d_ff_1_q), .D(d_ff_3_qn), .Q(d_ff_3_q), .Qn(d_ff_3_qn), .reset(Reset));  // open: preset, en
  not not_1 (not_1_out, Reset);
  not not_2 (not_2_out, d_ff_2_q);
  D_Flip_Flop d_ff_4 (.clk(d_ff_3_q), .D(d_ff_4_qn), .Q(d_ff_4_q), .Qn(d_ff_4_qn), .reset(Reset));  // open: preset, en
  xor xor_1 (xor_1_out, not_1_out, not_2_out);
  D_Flip_Flop d_ff_5 (.clk(d_ff_4_q), .D(d_ff_5_qn), .Q(d_ff_5_q), .Qn(d_ff_5_qn), .reset(Reset));  // open: preset, en
  and and_2 (and_2_out, xor_1_out, d_ff_9_q);
  D_Flip_Flop d_ff_6 (.clk(d_ff_5_q), .D(d_ff_6_qn), .Q(d_ff_6_q), .Qn(d_ff_6_qn), .reset(Reset));  // open: preset, en
  or or_1 (or_1_out, and_2_out, OK);
  D_Flip_Flop d_ff_7 (.clk(d_ff_8_q), .D(d_ff_7_qn), .Q(d_ff_7_q), .Qn(d_ff_7_qn), .reset(Reset));  // open: preset, en
  D_Flip_Flop d_ff_8 (.clk(d_ff_6_q), .D(d_ff_8_qn), .Q(d_ff_8_q), .Qn(d_ff_8_qn), .reset(Reset));  // open: preset, en
  D_Flip_Flop d_ff_9 (.clk(Takt), .D(or_1_out), .Q(d_ff_9_q), .reset(Reset));  // open: Qn, preset, en
  D_Flip_Flop d_ff_10 (
    .clk(d_ff_7_q), .D(d_ff_10_qn), .Q(d_ff_10_q), .Qn(d_ff_10_qn), .reset(Reset));  // open: preset, en
  D_Flip_Flop d_ff_11 (.clk(d_ff_10_q), .D(d_ff_11_qn), .Q(Start_ausgang), .Qn(d_ff_11_qn));  // open: preset, en, reset
endmodule
